# Fritzing sketch PowerLogger (saved by Fritzing 0.9.3b)

parts:
  Part1 = Arduino Micro (Rev3)
  U1 = LCD-16X2 [package=lcd-16x2]
  R1 = Resistor [tolerance=±5% resistance=220 package=THT]
  S1 = Toggle Switch [part_number="Recording button" package=THT]
  microSD_Transflash1 = SparkFun - microSD Transflash [part_number="microSD breakout Adafruit"]

nets:
  N1: Part1.MOSI, microSD_Transflash1.DI
  N2: Part1.RXLED/SS, microSD_Transflash1.CS
  N3: Part1.D1/TX, microSD_Transflash1.CD
  N4: Part1.GND, S1.COM
  N5: Part1.D5_PWM, S1.L1
  N6: Part1.D6_PWM/A7, U1.VO
  N7: Part1.D7, U1.DB7
  N8: Part1.D8_PWM/A8, U1.DB6
  N9: Part1.D9_PWM/A9, U1.DB5
  N10: Part1.D10_PWM/A10, U1.DB4
  N11: Part1.D11_PWM, U1.E
  N12: Part1.D12_PWM/A11, U1.RS
  N13: Part1.SCK, microSD_Transflash1.SCK
  N14: Part1.MISO, microSD_Transflash1.DO
  N15: U1.VDD, R1.Pin_0
  N16: U1.A, R1.Pin_1

notes:
  5V
  GND
  V+
  V-
  INA219
  RTC PCF8523
